# Fritzing sketch smartlock (saved by Fritzing 0.9.3b)

parts:
  KY-1 = Keyes Relay [package=THT]
  Part1 = RFID-RC522-v2
  Part2 = Arduino Uno (Rev3)
  L1 = Solenoid
  BAT1 = BC9VPC [package=bc9vpc]

nets:
  N1: KY-1.signal, Part2.D3_PWM
  N2: KY-1.power, Part2.5V
  GND: KY-1.ground, Part1.GND, Part2.GND
  N3: KY-1.C, L1.pin2
  N4: KY-1.NO, BAT1.V+
  N5: Part1.SDA, Part2.D10_PWM/SS
  N6: Part1.SCK, Part2.D13/SCK
  N7: Part1.MOSI, Part2.D11_PWM/MOSI
  N8: Part1.MISO, Part2.D12/MISO
  N9: Part1.RST, Part2.D7
  3.3V: Part1.3.3V, Part2.3V3
  N10: L1.pin1, BAT1.V-

custom parts:
  Keyes Relay: The Keyes 5V relay module is suitable for SCM development, home appliance control. It uses a 5V~12V TIL control signal which can control DC / AC signal.
  RFID-RC522-v2: A simple China made RFID-RC522 Reader; do check the pin labels, as this is a MFRC522 based clone.

// code stored in the sketch: bluetoothLight.ino
char blueToothVal;           //value sent over via bluetooth
char lastValue;              //stores last state of device (on/off)
 
void setup()
{
 Serial.begin(9600); 
 pinMode(13,OUTPUT);
 pinMode(12,INPUT);
}
 
 
void loop()
{
  if(Serial.available())
  {//if there is data being recieved
    blueToothVal=Serial.read(); //read it
  }
  if (blueToothVal=='n')
  {//if value from bluetooth serial is n
    digitalWrite(13,HIGH);            //switch on LED
    if (lastValue!='n')
      Serial.println(F("LED is on")); //print LED is on
    lastValue=blueToothVal;
  }
  else if (blueToothVal=='f')
  {//if value from bluetooth serial is n
    digitalWrite(13,LOW);             //turn off LED
    if (lastValue!='f')
      Serial.println(F("LED is off")); //print LED is on
    lastValue=blueToothVal;
  }
  delay(250);
}

// code stored in the sketch: locker.ino
//#include <ESP8266WiFi.h>
#include <SPI.h>
#include <MFRC522.h>
int in = 3;


#define RST_PIN 7   //D1 // Connect RST_PIN of RFID to D1
#define SDA_PIN 10  //D2 // Connect SDA_PIN of RFID to D2


MFRC522 rfid(SDA_PIN, RST_PIN);  // Create MFRC522 instance


void setup() {
  pinMode(in,OUTPUT);
  digitalWrite(in,HIGH);
  Serial.begin(9600);  // Initialize serial communication
  SPI.begin();         // Init SPI bus
  rfid.PCD_Init();     // Init MFRC522
  Serial.println("RFID Ready");
}


void loop() {
  // Look for new cards
  if (rfid.PICC_IsNewCardPresent() && rfid.PICC_ReadCardSerial()) {
    Serial.print("UID tag :");
    String content = "";


    // Read UID
    for (byte i = 0; i < rfid.uid.size; i++) {
      Serial.print(rfid.uid.uidByte[i] < 0x10 ? " 0" : " ");
      Serial.print(rfid.uid.uidByte[i], HEX);
      content.concat(String(rfid.uid.uidByte[i] < 0x10 ? " 0" : " "));
      content.concat(String(rfid.uid.uidByte[i], HEX));
    }


    Serial.println();
    //Serial.print("Message : ");
    content.toUpperCase();
    //Serial.println(content);


    if (content.substring(1) == "10 BF 22 2F") {
      Serial.println("ASSces Granted");
      delay(200);
      digitalWrite(in,LOW);
      delay(5000);
       digitalWrite(in,HIGH);
    } 
    else {
      Serial.println("Assces Dinied");
      delay(1000);
     
    
    }
  }
}
